# Fritzing sketch Chest (saved by Fritzing 1.0.6)

parts:
  M1 = DOIT Esp32 DevKit v1 (30 pins long, 11 pins width) [part_number=ESP32S-PIN30]
  R1 = Resistor [tolerance=±5% resistance=220 package="0603 [SMD]"]  # not connected
  D1 = Diode [package=diode-1n4148]
  Q1 = TRANSISTOR_NPN [package=to-92]  # not connected
  Part1 = InvenSense MPU6050
  LED1 = smd LED [color="Green (565nm)" package="0805 [SMD]"]  # not connected
  TP1 = TP4056 [chip_label=TP4056 package="DIP (Dual Inline) [THT]"]  # not connected
  BAT2 = 18650 battery holder [package=battery-18650-kit]  # not connected
  buz1 = Piezo Buzzer  # not connected
  S3 = Toggle Switch [package=THT]  # not connected

nets:
  N1: M1.3V3, D1.C
  GND: M1.GND, Part1.GND
  N2: M1.D21, Part1.SDA
  N3: M1.D22, Part1.SCL
  N4: D1.A, Part1.VCC

custom parts:
  DOIT Esp32 DevKit v1 (30 pins long, 11 pins width): The DOIT Esp32 DevKit v1 is one of the development board created by DOIT to evaluate the ESP-WROOM-32 module. It is based on the ESP32 microcontroller that boasts Wifi, Bluetooth, Ethernet and Low Power support all in a single chip. (vanepp) made breadboard work, adjusted pin numbering and labels and reduced size of schematic and cleaned up pcb. This chip is 30pins long (2 x15) and 11 pins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
  TP4056: A DIP stand-in part for whatever IC you want. With 6 pins on a 300mil dual inline package (DIP) footprint.
  18650 battery holder: 18650 Battery Holder identical to the dual battery version.
  Piezo Buzzer: Part from https://www.nutsvolts.com/magazine/article/november2012_SmileysWorkshop. Breadboard and icon images modified to be 0.3" in spacing and be more similar to the actual physical part.
