# Fritzing sketch Rangkaian perangkat keras SENDER_bab 5 (saved by Fritzing 1.0.6)

parts:
  MPU6050 = InvenSense MPU6050
  ESP32-C3 = LilyGo-T-OI-PLUS_1

nets:
  N1: MPU6050.VCC, ESP32-C3.connector7
  N2: MPU6050.GND, ESP32-C3.connector13
  N3: MPU6050.SCL, ESP32-C3.connector16
  N4: MPU6050.SDA, ESP32-C3.connector17
